# Fritzing sketch candle_schematic (saved by Fritzing 0.9.3b)
breadboards: 1

parts:
  Part1 = Intel Edison Arduinobreakout
  R1 = Resistor [tolerance=±5% resistance=470 package=THT]
  R2 = Resistor [tolerance=±5% resistance=470 package=THT]
  LED1 = LED - 5mm [color="Orange (620nm)" package="5 mm [THT]"]
  LED2 = LED - 5mm [color="Yellow (595nm)" package="5 mm [THT]"]
  Q1 = NPN-Transistor [package="TO92 [THT]"]
  R3 = Resistor [tolerance=±5% resistance=100 package=THT]
  R4 = Resistor [tolerance=±5% resistance=100 package=THT]
  Q2 = NPN-Transistor [package="TO92 [THT]"]

nets:
  N1: Part1.D5_PWM, R2.Pin_0
  N2: Part1.D6_PWM, R1.Pin_0
  N3: Part1.5V, R3.Pin_1, R4.Pin_1
  N4: Part1.GND, Q1.E, Q2.E
  N5: R1.Pin_1, Q2.B
  N6: R2.Pin_1, Q1.B
  N7: LED1.cathode, Q2.C
  N8: LED1.anode, R4.Pin_0
  N9: LED2.cathode, Q1.C
  N10: LED2.anode, R3.Pin_0
